// Logisim project ep3.circ as structural Verilog: 16 circuits, main circuit mainEP3
module PC (
  input  [7:0] Input,
  input  Load,
  input  Count_Up,
  output [7:0] Output
);

  wire and_1_out, and_2_out, and_3_out, and_4_out, and_5_out, and_6_out, and_7_out, and_8_out, and_9_out,
       and_10_out, and_11_out, and_12_out, and_13_out, and_14_out;

  and and_1 (and_1_out, Output[0], Output[1]);
  and and_2 (and_2_out, and_3_out, Output[6]);
  and and_3 (and_3_out, and_4_out, Output[5]);
  and and_4 (and_4_out, and_5_out, Output[4]);
  and and_5 (and_5_out, and_6_out, Output[3]);
  and and_6 (and_6_out, and_1_out, Output[2]);
  T_Flip_Flop t_ff_1 (.clk(Count_Up), .T(and_2_out), .Q(Output[7]), .preset(and_7_out), .reset(Load));  // open: Qn, en
  and and_7 (and_7_out, Load, Input[7]);
  T_Flip_Flop t_ff_2 (.clk(Count_Up), .T(and_3_out), .Q(Output[6]), .preset(and_8_out), .reset(Load));  // open: Qn, en
  T_Flip_Flop t_ff_3 (.clk(Count_Up), .T(and_4_out), .Q(Output[5]), .preset(and_9_out), .reset(Load));  // open: Qn, en
  T_Flip_Flop t_ff_4 (.clk(Count_Up), .T(and_5_out), .Q(Output[4]), .preset(and_10_out), .reset(Load));  // open: Qn, en
  T_Flip_Flop t_ff_5 (.clk(Count_Up), .T(and_6_out), .Q(Output[3]), .preset(and_11_out), .reset(Load));  // open: Qn, en
  T_Flip_Flop t_ff_6 (.clk(Count_Up), .T(and_1_out), .Q(Output[2]), .preset(and_12_out), .reset(Load));  // open: Qn, en
  T_Flip_Flop t_ff_7 (.clk(Count_Up), .T(Output[0]), .Q(Output[1]), .preset(and_13_out), .reset(Load));  // open: Qn, en
  T_Flip_Flop t_ff_8 (.clk(Count_Up), .T(1'b1), .Q(Output[0]), .preset(and_14_out), .reset(Load));  // open: Qn, en
  and and_8 (and_8_out, Load, Input[6]);
  and and_9 (and_9_out, Load, Input[5]);
  and and_10 (and_10_out, Load, Input[4]);
  and and_11 (and_11_out, Load, Input[3]);
  and and_12 (and_12_out, Load, Input[2]);
  and and_13 (and_13_out, Load, Input[1]);
  and and_14 (and_14_out, Load, Input[0]);
endmodule

module Selector (
  input  [7:0] in_1,
  output [3:0] out_2
);

  wire and_1_out, and_2_out, and_3_out, and_4_out, and_5_out, and_6_out, and_7_out, and_8_out, and_9_out,
       and_10_out, and_11_out, and_12_out, and_13_out, and_14_out, and_15_out, not_1_out, not_2_out,
       not_3_out, not_4_out, not_5_out, not_6_out, not_7_out, not_8_out, not_9_out, not_10_out, not_11_out,
       not_12_out, not_13_out, not_14_out, not_15_out, not_16_out, not_17_out, not_18_out, not_19_out,
       not_20_out, not_21_out, not_22_out, not_23_out, not_24_out, not_25_out, not_26_out, not_27_out,
       not_28_out, not_29_out, not_30_out, not_31_out, not_32_out, not_33_out, not_34_out, not_35_out,
       not_36_out, not_37_out, not_38_out, not_39_out, not_40_out, not_41_out, not_42_out, not_43_out,
       not_44_out, not_45_out, not_46_out, not_47_out, not_48_out, not_49_out, not_50_out, not_51_out,
       not_52_out, not_53_out, not_54_out, not_55_out, not_56_out, not_57_out, not_58_out, not_59_out,
       not_60_out;

  not not_1 (not_1_out, in_1[7]);
  not not_2 (not_2_out, in_1[6]);
  not not_3 (not_3_out, in_1[2]);
  not not_4 (not_4_out, in_1[1]);
  not not_5 (not_5_out, in_1[7]);
  not not_6 (not_6_out, in_1[6]);
  not not_7 (not_7_out, in_1[3]);
  not not_8 (not_8_out, in_1[7]);
  not not_9 (not_9_out, in_1[6]);
  not not_10 (not_10_out, in_1[5]);
  not not_11 (not_11_out, in_1[3]);
  not not_12 (not_12_out, in_1[7]);
  not not_13 (not_13_out, in_1[6]);
  not not_14 (not_14_out, in_1[3]);
  not not_15 (not_15_out, in_1[7]);
  not not_16 (not_16_out, in_1[6]);
  not not_17 (not_17_out, in_1[2]);
  not not_18 (not_18_out, in_1[1]);
  not not_19 (not_19_out, in_1[7]);
  not not_20 (not_20_out, in_1[5]);
  not not_21 (not_21_out, in_1[4]);
  not not_22 (not_22_out, in_1[3]);
  not not_23 (not_23_out, in_1[0]);
  not not_24 (not_24_out, in_1[7]);
  not not_25 (not_25_out, in_1[6]);
  not not_26 (not_26_out, in_1[5]);
  not not_27 (not_27_out, in_1[4]);
  not not_28 (not_28_out, in_1[1]);
  not not_29 (not_29_out, in_1[0]);
  not not_30 (not_30_out, in_1[7]);
  not not_31 (not_31_out, in_1[6]);
  not not_32 (not_32_out, in_1[5]);
  not not_33 (not_33_out, in_1[3]);
  not not_34 (not_34_out, in_1[7]);
  not not_35 (not_35_out, in_1[6]);
  not not_36 (not_36_out, in_1[3]);
  not not_37 (not_37_out, in_1[2]);
  not not_38 (not_38_out, in_1[7]);
  not not_39 (not_39_out, in_1[6]);
  not not_40 (not_40_out, in_1[3]);
  not not_41 (not_41_out, in_1[1]);
  not not_42 (not_42_out, in_1[7]);
  not not_43 (not_43_out, in_1[6]);
  not not_44 (not_44_out, in_1[2]);
  not not_45 (not_45_out, in_1[1]);
  not not_46 (not_46_out, in_1[7]);
  not not_47 (not_47_out, in_1[6]);
  not not_48 (not_48_out, in_1[5]);
  not not_49 (not_49_out, in_1[4]);
  not not_50 (not_50_out, in_1[2]);
  not not_51 (not_51_out, in_1[7]);
  not not_52 (not_52_out, in_1[6]);
  not not_53 (not_53_out, in_1[3]);
  not not_54 (not_54_out, in_1[7]);
  not not_55 (not_55_out, in_1[6]);
  not not_56 (not_56_out, in_1[2]);
  not not_57 (not_57_out, in_1[1]);
  not not_58 (not_58_out, in_1[7]);
  not not_59 (not_59_out, in_1[6]);
  not not_60 (not_60_out, in_1[3]);
  and and_1 (and_1_out, not_1_out, not_2_out, in_1[4], in_1[3], not_3_out, not_4_out);
  and and_2 (and_2_out, not_5_out, not_6_out, in_1[5], in_1[4], not_7_out, in_1[2]);
  and and_3 (and_3_out, not_8_out, not_9_out, not_10_out, in_1[4], not_11_out, in_1[2], in_1[0]);
  and and_4 (and_4_out, not_12_out, not_13_out, in_1[4], not_14_out, in_1[2], in_1[1]);
  and and_5 (and_5_out, not_15_out, not_16_out, in_1[5], in_1[4], in_1[3], not_17_out, not_18_out);
  and and_6 (and_6_out, not_19_out, in_1[6], not_20_out, not_21_out, not_22_out, in_1[2], in_1[1], not_23_out);
  and and_7 (and_7_out, not_24_out, not_25_out, not_26_out, not_27_out, in_1[3], in_1[2], not_28_out, not_29_out);
  and and_8 (and_8_out, not_30_out, not_31_out, not_32_out, in_1[4], not_33_out, in_1[2], in_1[1]);
  and and_9 (and_9_out, not_34_out, not_35_out, in_1[5], in_1[4], not_36_out, not_37_out, in_1[1], in_1[0]);
  and and_10 (and_10_out, not_38_out, not_39_out, in_1[5], in_1[4], not_40_out, in_1[2], not_41_out);
  and and_11 (and_11_out, not_42_out, not_43_out, in_1[5], in_1[4], in_1[3], not_44_out, not_45_out);
  and and_12 (and_12_out, not_46_out, not_47_out, not_48_out, not_49_out, in_1[3], not_50_out, in_1[1], in_1[0]);
  and and_13 (and_13_out, not_51_out, not_52_out, in_1[4], not_53_out, in_1[2], in_1[0]);
  and and_14 (and_14_out, not_54_out, not_55_out, in_1[4], in_1[3], not_56_out, not_57_out, in_1[0]);
  and and_15 (and_15_out, not_58_out, not_59_out, in_1[5], in_1[4], not_60_out, in_1[1], in_1[0]);
  or or_1 (out_2[3], and_1_out, and_2_out);
  or or_2 (out_2[2], and_3_out, and_4_out, and_5_out, and_6_out);
  or or_3 (out_2[1], and_7_out, and_8_out, and_9_out, and_10_out, and_11_out);
  or or_4 (out_2[0], and_12_out, and_13_out, and_14_out, and_15_out);
endmodule

module CTRL (
  input  [15:0] RAM,
  input  [15:0] Accumulator,
  input  [15:0] INPUT_IR,
  input  Clock,
  output NOP,
  output [15:0] Output_Data2Acc,
  output [15:0] Output_Acc2Add,
  output Stop,
  output [15:0] \Acc_operação ,
  output [7:0] Conditional_Jump,
  output [7:0] Address,
  output [2:0] OP_Selector,
  output Read_Write,
  output Accumulator_Clock,
  output Memory_Clock,
  output PCLoad_Clock,
  output IRPC_CLock
);

  wire protector_1_a, protector_1_m, protector_1_p, t_ff_1_q, t_ff_5_q, t_ff_5_qn;
  wire [2:0] selector_mux_jmpc_1_out_2;
  wire [3:0] selector_1_out_2;
  wire [5:0] condicional_1_out_2;
  wire [15:0] controlled_buffer_1_out, controlled_buffer_2_out, controlled_buffer_3_out,
       controlled_buffer_4_out, controlled_buffer_5_out, controlled_buffer_6_out, demultiplexer_1_out3,
       demultiplexer_1_out5, demultiplexer_1_out6, demultiplexer_1_out7, demultiplexer_1_out8,
       demultiplexer_1_out9, demultiplexer_1_out10, demultiplexer_1_out11, demultiplexer_1_out12,
       demultiplexer_1_out13, demultiplexer_1_out14, demultiplexer_1_out15, multiplexer_1_out;
  wire [15:1] demultiplexer_1_out0, demultiplexer_1_out4;
  wire [15:8] multiplexer_2_out;

  Selector_MUX_jmpC selector_mux_jmpc_1 (.in_1(INPUT_IR[15:8]), .out_2(selector_mux_jmpc_1_out_2));
  Selector_OP selector_op_1 (.in_1(INPUT_IR[15:8]), .out_2(OP_Selector));
  protector protector_1 (.a(protector_1_a), .m(protector_1_m), .p(protector_1_p), .in_1(INPUT_IR[15:8]));
  Multiplexer #(.select(4), .width(16), .enable("false")) multiplexer_1 (
    .in0(16'h1), .in1(RAM), .in2(Accumulator), .in3(INPUT_IR), .in4(16'h1), .in5(Accumulator),
    .in6(Accumulator), .in7(Accumulator), .in8(Accumulator), .in9(Accumulator), .in10(INPUT_IR),
    .in11(INPUT_IR), .in12(INPUT_IR), .in13(INPUT_IR), .in14(INPUT_IR), .in15(INPUT_IR),
    .out(multiplexer_1_out), .sel(selector_1_out_2));
  Selector selector_1 (.in_1(INPUT_IR[15:8]), .out_2(selector_1_out_2));
  Selector_Accum selector_accum_1 (.In(INPUT_IR[15:8]), .Out(Read_Write));
  Demultiplexer #(.select(4), .width(16), .enable("false")) demultiplexer_1 (
    .out0({demultiplexer_1_out0, NOP}), .out1(Output_Data2Acc), .out2(Output_Acc2Add),
    .out3(demultiplexer_1_out3), .out4({demultiplexer_1_out4, Stop}), .out5(demultiplexer_1_out5),
    .out6(demultiplexer_1_out6), .out7(demultiplexer_1_out7), .out8(demultiplexer_1_out8),
    .out9(demultiplexer_1_out9), .out10(demultiplexer_1_out10), .out11(demultiplexer_1_out11),
    .out12(demultiplexer_1_out12), .out13(demultiplexer_1_out13), .out14(demultiplexer_1_out14),
    .out15(demultiplexer_1_out15), .in(multiplexer_1_out), .sel(selector_1_out_2));
  assign controlled_buffer_1_out = condicional_1_out_2[0] ? demultiplexer_1_out10 : 16'bz;  // Controlled_Buffer controlled_buffer_1
  Condicional condicional_1 (.Input(Accumulator), .out_2(condicional_1_out_2));
  T_Flip_Flop t_ff_1 (.clk(Clock), .T(t_ff_5_q), .Q(t_ff_1_q), .reset(protector_1_a));  // open: Qn, preset, en
  T_Flip_Flop t_ff_2 (.clk(Clock), .T(1'b1), .Q(Memory_Clock), .reset(protector_1_m));  // open: Qn, preset, en
  T_Flip_Flop t_ff_3 (.clk(Clock), .T(1'b1), .Q(PCLoad_Clock), .reset(protector_1_p));  // open: Qn, preset, en
  T_Flip_Flop t_ff_4 (.clk(Clock), .T(1'b1), .Q(IRPC_CLock));  // open: Qn, preset, reset, en
  assign controlled_buffer_2_out = condicional_1_out_2[1] ? demultiplexer_1_out11 : 16'bz;  // Controlled_Buffer controlled_buffer_2
  assign controlled_buffer_3_out = condicional_1_out_2[2] ? demultiplexer_1_out12 : 16'bz;  // Controlled_Buffer controlled_buffer_3
  assign controlled_buffer_4_out = condicional_1_out_2[3] ? demultiplexer_1_out13 : 16'bz;  // Controlled_Buffer controlled_buffer_4
  assign controlled_buffer_5_out = condicional_1_out_2[4] ? demultiplexer_1_out14 : 16'bz;  // Controlled_Buffer controlled_buffer_5
  T_Flip_Flop t_ff_5 (.clk(Clock), .T(1'b1), .Q(t_ff_5_q), .Qn(t_ff_5_qn), .reset(protector_1_a));  // open: preset, en
  assign controlled_buffer_6_out = condicional_1_out_2[5] ? demultiplexer_1_out15 : 16'bz;  // Controlled_Buffer controlled_buffer_6
  and and_1 (Accumulator_Clock, t_ff_1_q, t_ff_5_qn);
  Multiplexer #(.select(3), .width(16), .enable("false")) multiplexer_2 (
    .in1(controlled_buffer_1_out), .in2(controlled_buffer_2_out), .in3(controlled_buffer_3_out),
    .in4(controlled_buffer_4_out), .in5(controlled_buffer_5_out), .in6(controlled_buffer_6_out),
    .in7(demultiplexer_1_out3), .out({multiplexer_2_out, Conditional_Jump}), .sel(selector_mux_jmpc_1_out_2));  // open: in0
  Multiplexer #(.select(3), .width(16)) multiplexer_3 (
    .in1(demultiplexer_1_out5), .in2(demultiplexer_1_out6), .in3(demultiplexer_1_out7),
    .in4(demultiplexer_1_out8), .in5(demultiplexer_1_out9), .out(\Acc_operação ), .sel(OP_Selector));  // open: in0, in6, in7, en

  assign Address = INPUT_IR[7:0];

  // Other names for the same wires on the sheet: CFlags[15:0] = Accumulator; false[7:0] = INPUT_IR[7:0]

  // Notes on the sheet:
  //   3 Entradas
  //   7 Saidas
  //   RAM D
  //   Accumulator
  //   RAM A
endmodule

module FF_clock (
  input  IN,
  output OUT
);

  wire t_ff_2_q;

  T_Flip_Flop t_ff_1 (.clk(IN), .T(t_ff_2_q), .Q(OUT));  // open: Qn, preset, reset, en
  T_Flip_Flop t_ff_2 (.clk(IN), .T(1'b1), .Q(t_ff_2_q));  // open: Qn, preset, reset, en
endmodule

// C
module First (
  input  Clock,
  output OK
);

  Counter #(.width(2), .max('h2), .ongoal("stay")) counter_1 (.carry(OK), .clk(Clock));  // open: load, D, count, Q, clr
endmodule

module Selector_MUX (
  input  in_1,
  input  in_2,
  output out_3
);

  wire and_1_out, and_2_out;

  and and_1 (and_1_out, ~in_1, ~in_2);  // AND_Gate
  and and_2 (and_2_out, in_1, in_2);
  or or_1 (out_3, and_1_out, and_2_out);
endmodule

module Condicional (
  input  [15:0] Input,
  output [5:0] out_2
);

  wire comparator_1_gt, comparator_1_lt;

  Comparator #(.width(16)) comparator_1 (
    .a(Input), .b({16{1'b0}}), .gt(comparator_1_gt), .eq(out_2[2]), .lt(comparator_1_lt));
  not not_1 (out_2[4], out_2[2]);
  or _0 (out_2[0], comparator_1_gt, out_2[2]);
  and _0_2 (out_2[3], comparator_1_gt, ~out_2[2]);  // AND_Gate
  and _0_3 (out_2[1], comparator_1_lt, ~out_2[2]);  // AND_Gate
  or _0_4 (out_2[5], out_2[2], comparator_1_lt);

  // Notes on the sheet:
  //   = 0
  //   != 0
endmodule

module ALU (
  input  [15:0] A,
  input  [15:0] B,
  input  [2:0] in_3,
  output [15:0] \Saída ,
  output Overflow,
  output Flag_Div_p__0
);

  wire adder_1_cout, adder_2_cout, and_1_out, and_2_out, and_3_out, and_4_out, and_5_out, and_7_out,
       and_8_out, comparator_1_eq, comparator_2_eq, not_1_out;
  wire [15:0] adder_1_out, adder_2_out, divider_1_out, divider_1_rem, multiplier_1_cout, multiplier_1_out,
       negator_1_out;

  Negator #(.width(16)) negator_1 (.in(B), .out(negator_1_out));
  Adder #(.width(16)) adder_1 (.a(A), .b(B), .out(adder_1_out), .cout(adder_1_cout));  // open: cin
  Adder #(.width(16)) adder_2 (.a(A), .b(negator_1_out), .out(adder_2_out), .cin(1'b1), .cout(adder_2_cout));
  Multiplier #(.width(16)) multiplier_1 (.a(A), .b(B), .out(multiplier_1_out), .cout(multiplier_1_cout));  // open: cin
  Divider #(.width(16)) divider_1 (.a(A), .b(B), .out(divider_1_out), .rem(divider_1_rem));  // open: upper
  not not_1 (not_1_out, comparator_1_eq);
  Comparator #(.width(16)) comparator_1 (.a(multiplier_1_cout), .b({16{1'b0}}), .eq(comparator_1_eq));  // open: gt, lt
  Comparator #(.width(16)) comparator_2 (.a(B), .b({16{1'b0}}), .eq(comparator_2_eq));  // open: gt, lt
  Multiplexer #(.select(3), .width(16), .enable("false")) multiplexer_1 (
    .in1(adder_1_out), .in2(adder_2_out), .in3(multiplier_1_out), .in4(divider_1_out), .in5(divider_1_rem),
    .out(\Saída ), .sel(in_3));  // open: in0, in6, in7
  and and_1 (and_1_out, in_3[0], ~in_3[1], ~in_3[2]);  // AND_Gate
  and and_2 (and_2_out, ~in_3[0], in_3[1], ~in_3[2]);  // AND_Gate
  and and_3 (and_3_out, in_3[0], in_3[1], ~in_3[2]);  // AND_Gate
  and and_4 (and_4_out, and_3_out, not_1_out);
  and and_5 (and_5_out, ~in_3[0], ~in_3[1], in_3[2]);  // AND_Gate
  and and_6 (Flag_Div_p__0, and_5_out, comparator_2_eq);
  and and_7 (and_7_out, and_1_out, adder_1_cout);
  and and_8 (and_8_out, and_2_out, adder_2_cout);
  or or_1 (Overflow, and_7_out, and_8_out, and_4_out);

  // Notes on the sheet:
  //   Ovf Soma
  //   Ovf Sub
  //   Ovf Mult
  //   Div. p/ 0
endmodule

module Selector_OP (
  input  [7:0] in_1,
  output [2:0] out_2
);

  wire and_3_out, and_4_out, not_1_out, not_2_out, not_3_out, not_4_out, not_5_out, not_6_out, not_7_out,
       not_8_out, not_9_out, not_10_out, not_11_out, not_12_out, not_13_out, not_14_out, not_15_out,
       not_16_out, not_17_out, not_18_out;

  not not_1 (not_1_out, in_1[7]);
  not not_2 (not_2_out, in_1[6]);
  not not_3 (not_3_out, in_1[5]);
  not not_4 (not_4_out, in_1[2]);
  not not_5 (not_5_out, in_1[1]);
  not not_6 (not_6_out, in_1[7]);
  not not_7 (not_7_out, in_1[6]);
  not not_8 (not_8_out, in_1[5]);
  not not_9 (not_9_out, in_1[3]);
  not not_10 (not_10_out, in_1[7]);
  not not_11 (not_11_out, in_1[6]);
  not not_12 (not_12_out, in_1[5]);
  not not_13 (not_13_out, in_1[3]);
  not not_14 (not_14_out, in_1[7]);
  not not_15 (not_15_out, in_1[6]);
  not not_16 (not_16_out, in_1[5]);
  not not_17 (not_17_out, in_1[2]);
  not not_18 (not_18_out, in_1[1]);
  and and_1 (out_2[2], not_1_out, not_2_out, not_3_out, in_1[4], in_1[3], not_4_out, not_5_out);
  and and_2 (out_2[1], not_6_out, not_7_out, not_8_out, in_1[4], not_9_out, in_1[2], in_1[1]);
  and and_3 (and_3_out, not_10_out, not_11_out, not_12_out, in_1[4], not_13_out, in_1[2], in_1[0]);
  and and_4 (and_4_out, not_14_out, not_15_out, not_16_out, in_1[4], in_1[3], not_17_out, not_18_out, in_1[0]);
  or or_1 (out_2[0], and_3_out, and_4_out);
endmodule

// Acum
module Acumulator (
  input  [15:0] In,
  input  Clear,
  input  in_3,
  input  Clock,
  output [15:0] Out
);

  Register #(.width(16)) register_1 (.D(In), .en(in_3), .Q(Out), .clk(Clock), .clr(Clear));
endmodule

module I_O_Controller (
  input  [7:0] in_1,
  output [1:0] out_2
);

  wire not_1_out, not_2_out, not_3_out, not_4_out, not_5_out, not_6_out, not_7_out, not_8_out;

  not not_1 (not_1_out, in_1[7]);
  not not_2 (not_2_out, in_1[6]);
  not not_3 (not_3_out, in_1[4]);
  not not_4 (not_4_out, in_1[2]);
  not not_5 (not_5_out, in_1[1]);
  not not_6 (not_6_out, in_1[7]);
  not not_7 (not_7_out, in_1[6]);
  not not_8 (not_8_out, in_1[5]);
  and and_1 (out_2[1], not_1_out, not_2_out, in_1[5], not_3_out, in_1[3], not_4_out, not_5_out, in_1[0]);
  and and_2 (out_2[0], not_6_out, not_7_out, not_8_out, in_1[4], in_1[3], in_1[2], in_1[1], in_1[0]);
endmodule

module mainEP3 (
);

  wire and_1_out, clock_1_out, ctrl_1_accumulator_clock, ctrl_1_memory_clock, ctrl_1_nop,
       ctrl_1_pcload_clock, ctrl_1_read_write, ctrl_1_stop, NOP, PCClock, start_1_out_2;
  wire [2:0] ctrl_1_op_selector;
  wire [7:0] ctrl_1_address, ctrl_1_conditional_jump, multiplexer_1_out, pc_1_output;
  wire [15:0] acumulator_1_out, \alu_1_saída , \ctrl_1_acc_operação , ctrl_1_output_acc2add,
       ctrl_1_output_data2acc, IR_q, multiplexer_2_out, ram_1_data;

  Multiplexer #(.width(8), .enable("false")) multiplexer_1 (
    .in0(pc_1_output), .in1(ctrl_1_address), .out(multiplexer_1_out), .sel(start_1_out_2));
  PC pc_1 (.Output(pc_1_output), .Count_Up(PCClock), .Input(ctrl_1_conditional_jump), .Load(ctrl_1_pcload_clock));
  Start start_1 (.in_1(and_1_out), .out_2(start_1_out_2));
  RAM #(.dataWidth(16), .bus("separate")) ram_1 (
    .addr(multiplexer_1_out), .din(ctrl_1_output_acc2add), .data(ram_1_data), .str(NOP),
    .clk(ctrl_1_memory_clock));  // open: sel, ld, clr
  and and_1 (and_1_out, ~ctrl_1_stop, clock_1_out);  // AND_Gate
  Register #(.width(16)) IR (.D(ram_1_data), .Q(IR_q), .clk(PCClock));  // open: en, clr
  CTRL ctrl_1 (
    .RAM(ram_1_data), .Accumulator(acumulator_1_out), .INPUT_IR(IR_q),
    .Output_Data2Acc(ctrl_1_output_data2acc), .Output_Acc2Add(ctrl_1_output_acc2add),
    .Address(ctrl_1_address), .NOP(ctrl_1_nop), .Clock(and_1_out),
    .Accumulator_Clock(ctrl_1_accumulator_clock), .Memory_Clock(ctrl_1_memory_clock),
    .PCLoad_Clock(ctrl_1_pcload_clock), .IRPC_CLock(PCClock), .Stop(ctrl_1_stop),
    .\Acc_operação (\ctrl_1_acc_operação ), .Conditional_Jump(ctrl_1_conditional_jump),
    .OP_Selector(ctrl_1_op_selector), .Read_Write(ctrl_1_read_write));
  Clock clock_1 (.out(clock_1_out));
  not not_1 (NOP, ctrl_1_nop);
  ALU alu_1 (
    .\Saída (\alu_1_saída ), .A(acumulator_1_out), .B(\ctrl_1_acc_operação ), .in_3(ctrl_1_op_selector));  // open: Overflow, Flag_Div_p__0
  Multiplexer #(.width(16), .enable("false")) multiplexer_2 (
    .in0(ctrl_1_output_data2acc), .in1(\alu_1_saída ), .out(multiplexer_2_out), .sel(ctrl_1_read_write));
  Acumulator acumulator_1 (
    .In(multiplexer_2_out), .Out(acumulator_1_out), .Clock(ctrl_1_accumulator_clock), .in_3(NOP));  // open: Clear
endmodule

module Start (
  input  in_1,
  output out_2
);

  wire counter_1_q, selector_mux_1_out_3;

  not not_1 (out_2, selector_mux_1_out_3);
  Selector_MUX selector_mux_1 (.in_1(counter_1_q), .in_2(in_1), .out_3(selector_mux_1_out_3));
  Counter #(.width(1), .max('h1)) counter_1 (.Q(counter_1_q), .clk(in_1));  // open: load, D, count, carry, clr
endmodule

// JmpC
module Selector_MUX_jmpC (
  input  [7:0] in_1,
  output [2:0] out_2
);

  wire and_1_out, and_2_out, and_3_out, and_4_out, and_5_out, and_6_out, and_7_out, and_8_out, and_9_out,
       not_1_out, not_2_out, not_3_out, not_4_out, not_5_out, not_6_out, not_7_out, not_8_out, not_9_out,
       not_10_out, not_11_out, not_12_out, not_13_out, not_14_out, not_15_out, not_16_out, not_17_out,
       not_18_out, not_19_out, not_20_out, not_21_out, not_22_out, not_23_out, not_24_out, not_25_out,
       not_26_out, not_27_out, not_28_out, not_29_out, not_30_out, not_31_out, not_32_out, not_33_out,
       not_34_out, not_35_out, not_36_out;

  not not_1 (not_1_out, in_1[7]);
  not not_2 (not_2_out, in_1[6]);
  not not_3 (not_3_out, in_1[3]);
  not not_4 (not_4_out, in_1[7]);
  not not_5 (not_5_out, in_1[6]);
  not not_6 (not_6_out, in_1[2]);
  not not_7 (not_7_out, in_1[1]);
  not not_8 (not_8_out, in_1[7]);
  not not_9 (not_9_out, in_1[6]);
  not not_10 (not_10_out, in_1[3]);
  not not_11 (not_11_out, in_1[2]);
  not not_12 (not_12_out, in_1[7]);
  not not_13 (not_13_out, in_1[6]);
  not not_14 (not_14_out, in_1[3]);
  not not_15 (not_15_out, in_1[1]);
  not not_16 (not_16_out, in_1[7]);
  not not_17 (not_17_out, in_1[6]);
  not not_18 (not_18_out, in_1[3]);
  not not_19 (not_19_out, in_1[0]);
  not not_20 (not_20_out, in_1[7]);
  not not_21 (not_21_out, in_1[6]);
  not not_22 (not_22_out, in_1[2]);
  not not_23 (not_23_out, in_1[1]);
  not not_24 (not_24_out, in_1[7]);
  not not_25 (not_25_out, in_1[6]);
  not not_26 (not_26_out, in_1[3]);
  not not_27 (not_27_out, in_1[2]);
  not not_28 (not_28_out, in_1[7]);
  not not_29 (not_29_out, in_1[6]);
  not not_30 (not_30_out, in_1[3]);
  not not_31 (not_31_out, in_1[0]);
  not not_32 (not_32_out, in_1[7]);
  not not_33 (not_33_out, in_1[6]);
  not not_34 (not_34_out, in_1[2]);
  not not_35 (not_35_out, in_1[1]);
  not not_36 (not_36_out, in_1[0]);
  and and_1 (and_1_out, not_1_out, not_2_out, in_1[5], in_1[4], not_3_out, in_1[1], in_1[0]);
  and and_2 (and_2_out, not_4_out, not_5_out, in_1[5], in_1[4], in_1[3], not_6_out, not_7_out);
  and and_3 (and_3_out, not_8_out, not_9_out, in_1[5], in_1[4], not_10_out, not_11_out, in_1[1], in_1[0]);
  and and_4 (and_4_out, not_12_out, not_13_out, in_1[5], in_1[4], not_14_out, in_1[2], not_15_out, in_1[0]);
  and and_5 (and_5_out, not_16_out, not_17_out, in_1[5], in_1[4], not_18_out, in_1[2], in_1[1], not_19_out);
  and and_6 (and_6_out, not_20_out, not_21_out, in_1[5], in_1[4], in_1[3], not_22_out, not_23_out, in_1[0]);
  and and_7 (and_7_out, not_24_out, not_25_out, in_1[5], in_1[4], not_26_out, not_27_out, in_1[1], in_1[0]);
  and and_8 (and_8_out, not_28_out, not_29_out, in_1[5], in_1[4], not_30_out, in_1[2], not_31_out);
  and and_9 (and_9_out, not_32_out, not_33_out, in_1[5], in_1[4], in_1[3], not_34_out, not_35_out, not_36_out);
  or or_1 (out_2[2], and_1_out, and_2_out);
  or or_2 (out_2[1], and_3_out, and_4_out, and_5_out, and_6_out);
  or or_3 (out_2[0], and_7_out, and_8_out, and_9_out);
endmodule

module Selector_Accum (
  input  [7:0] In,
  output Out
);

  wire and_1_out, and_2_out, and_3_out, not_1_out, not_2_out, not_3_out, not_4_out, not_5_out, not_6_out,
       not_7_out, not_8_out, not_9_out, not_10_out, not_11_out, not_12_out, not_13_out;

  not not_1 (not_1_out, In[7]);
  not not_2 (not_2_out, In[6]);
  not not_3 (not_3_out, In[5]);
  not not_4 (not_4_out, In[3]);
  not not_5 (not_5_out, In[7]);
  not not_6 (not_6_out, In[6]);
  not not_7 (not_7_out, In[5]);
  not not_8 (not_8_out, In[3]);
  not not_9 (not_9_out, In[7]);
  not not_10 (not_10_out, In[6]);
  not not_11 (not_11_out, In[5]);
  not not_12 (not_12_out, In[2]);
  not not_13 (not_13_out, In[1]);
  and and_1 (and_1_out, not_1_out, not_2_out, not_3_out, In[4], not_4_out, In[2], In[0]);
  and and_2 (and_2_out, not_5_out, not_6_out, not_7_out, In[4], not_8_out, In[2], In[1]);
  and and_3 (and_3_out, not_9_out, not_10_out, not_11_out, In[4], In[3], not_12_out, not_13_out);
  or or_1 (Out, and_1_out, and_2_out, and_3_out);
endmodule

module protector (
  input  [7:0] in_1,
  output a,
  output m,
  output p
);

  wire and_1_out, and_2_out, and_3_out, and_4_out, and_5_out, and_6_out, and_7_out, and_8_out, and_9_out,
       and_10_out, and_11_out, and_12_out, and_13_out, and_14_out, and_15_out, and_16_out, and_17_out,
       and_18_out, and_19_out, and_20_out, not_1_out, not_2_out, not_3_out, not_4_out, not_5_out, not_6_out,
       not_7_out, not_8_out, not_9_out, not_10_out, not_11_out, not_12_out, not_13_out, not_14_out,
       not_15_out, not_16_out, not_17_out, not_18_out, not_19_out, not_20_out, not_21_out, not_22_out,
       not_23_out, not_24_out, not_25_out, not_26_out, not_27_out, not_28_out, not_29_out, not_30_out,
       not_31_out, not_32_out, not_33_out, not_34_out, not_35_out, not_36_out, not_37_out, not_38_out,
       not_39_out, not_40_out, not_41_out, not_42_out, not_43_out, not_44_out, not_45_out, not_46_out,
       not_47_out, not_48_out, not_49_out, not_50_out, not_51_out, not_52_out, not_53_out, not_54_out,
       not_55_out, not_56_out, not_57_out, not_58_out, not_59_out, not_60_out, not_61_out, not_62_out,
       not_63_out, not_64_out, not_65_out, not_66_out, not_67_out, not_68_out, not_69_out, not_70_out,
       not_71_out, not_72_out, not_73_out, not_74_out, not_75_out, not_76_out, not_77_out, not_78_out,
       not_79_out, not_80_out, not_81_out, not_82_out, not_83_out, not_84_out, not_85_out, not_86_out,
       not_87_out, not_88_out;

  not not_1 (not_1_out, in_1[7]);
  not not_2 (not_2_out, in_1[6]);
  not not_3 (not_3_out, in_1[5]);
  not not_4 (not_4_out, in_1[4]);
  not not_5 (not_5_out, in_1[1]);
  not not_6 (not_6_out, in_1[0]);
  not not_7 (not_7_out, in_1[7]);
  not not_8 (not_8_out, in_1[6]);
  not not_9 (not_9_out, in_1[3]);
  not not_10 (not_10_out, in_1[7]);
  not not_11 (not_11_out, in_1[6]);
  not not_12 (not_12_out, in_1[3]);
  not not_13 (not_13_out, in_1[7]);
  not not_14 (not_14_out, in_1[6]);
  not not_15 (not_15_out, in_1[2]);
  not not_16 (not_16_out, in_1[1]);
  not not_17 (not_17_out, in_1[0]);
  not not_18 (not_18_out, in_1[6]);
  not not_19 (not_19_out, in_1[5]);
  not not_20 (not_20_out, in_1[4]);
  not not_21 (not_21_out, in_1[3]);
  not not_22 (not_22_out, in_1[0]);
  not not_23 (not_23_out, in_1[7]);
  not not_24 (not_24_out, in_1[6]);
  not not_25 (not_25_out, in_1[5]);
  not not_26 (not_26_out, in_1[4]);
  not not_27 (not_27_out, in_1[2]);
  not not_28 (not_28_out, in_1[7]);
  not not_29 (not_29_out, in_1[6]);
  not not_30 (not_30_out, in_1[3]);
  not not_31 (not_31_out, in_1[7]);
  not not_32 (not_32_out, in_1[6]);
  not not_33 (not_33_out, in_1[3]);
  not not_34 (not_34_out, in_1[7]);
  not not_35 (not_35_out, in_1[6]);
  not not_36 (not_36_out, in_1[5]);
  not not_37 (not_37_out, in_1[2]);
  not not_38 (not_38_out, in_1[1]);
  not not_39 (not_39_out, in_1[7]);
  not not_40 (not_40_out, in_1[6]);
  not not_41 (not_41_out, in_1[2]);
  not not_42 (not_42_out, in_1[1]);
  not not_43 (not_43_out, in_1[0]);
  not not_44 (not_44_out, in_1[7]);
  not not_45 (not_45_out, in_1[6]);
  not not_46 (not_46_out, in_1[3]);
  not not_47 (not_47_out, in_1[7]);
  not not_48 (not_48_out, in_1[6]);
  not not_49 (not_49_out, in_1[3]);
  not not_50 (not_50_out, in_1[6]);
  not not_51 (not_51_out, in_1[5]);
  not not_52 (not_52_out, in_1[4]);
  not not_53 (not_53_out, in_1[3]);
  not not_54 (not_54_out, in_1[0]);
  not not_55 (not_55_out, in_1[7]);
  not not_56 (not_56_out, in_1[6]);
  not not_57 (not_57_out, in_1[5]);
  not not_58 (not_58_out, in_1[4]);
  not not_59 (not_59_out, in_1[2]);
  not not_60 (not_60_out, in_1[7]);
  not not_61 (not_61_out, in_1[6]);
  not not_62 (not_62_out, in_1[5]);
  not not_63 (not_63_out, in_1[4]);
  not not_64 (not_64_out, in_1[1]);
  not not_65 (not_65_out, in_1[0]);
  not not_66 (not_66_out, in_1[7]);
  not not_67 (not_67_out, in_1[6]);
  not not_68 (not_68_out, in_1[5]);
  not not_69 (not_69_out, in_1[3]);
  not not_70 (not_70_out, in_1[7]);
  not not_71 (not_71_out, in_1[6]);
  not not_72 (not_72_out, in_1[5]);
  not not_73 (not_73_out, in_1[3]);
  not not_74 (not_74_out, in_1[7]);
  not not_75 (not_75_out, in_1[6]);
  not not_76 (not_76_out, in_1[5]);
  not not_77 (not_77_out, in_1[2]);
  not not_78 (not_78_out, in_1[1]);
  not not_79 (not_79_out, in_1[7]);
  not not_80 (not_80_out, in_1[6]);
  not not_81 (not_81_out, in_1[3]);
  not not_82 (not_82_out, in_1[2]);
  not not_83 (not_83_out, in_1[0]);
  not not_84 (not_84_out, in_1[6]);
  not not_85 (not_85_out, in_1[5]);
  not not_86 (not_86_out, in_1[4]);
  not not_87 (not_87_out, in_1[3]);
  not not_88 (not_88_out, in_1[0]);
  and and_1 (and_1_out, not_1_out, not_2_out, not_3_out, not_4_out, in_1[3], in_1[2], not_5_out, not_6_out);
  and and_2 (and_2_out, not_7_out, not_8_out, in_1[5], in_1[4], not_9_out, in_1[1]);
  and and_3 (and_3_out, not_10_out, not_11_out, in_1[5], in_1[4], not_12_out, in_1[2]);
  and and_4 (and_4_out, not_13_out, not_14_out, in_1[5], in_1[4], in_1[3], not_15_out, not_16_out, not_17_out);
  and and_5 (and_5_out, in_1[7], not_18_out, not_19_out, not_20_out, not_21_out, in_1[2], in_1[1], not_22_out);
  and and_6 (and_6_out, not_23_out, not_24_out, not_25_out, not_26_out, in_1[3], not_27_out, in_1[1], in_1[0]);
  and and_7 (and_7_out, not_28_out, not_29_out, in_1[4], not_30_out, in_1[2], in_1[0]);
  and and_8 (and_8_out, not_31_out, not_32_out, in_1[4], not_33_out, in_1[2], in_1[1]);
  and and_9 (and_9_out, not_34_out, not_35_out, not_36_out, in_1[4], in_1[3], not_37_out, not_38_out);
  and and_10 (and_10_out, not_39_out, not_40_out, in_1[4], in_1[3], not_41_out, not_42_out, not_43_out);
  and and_11 (and_11_out, not_44_out, not_45_out, in_1[5], in_1[4], not_46_out, in_1[1]);
  and and_12 (and_12_out, not_47_out, not_48_out, in_1[5], in_1[4], not_49_out, in_1[2]);
  and and_13 (and_13_out, in_1[7], not_50_out, not_51_out, not_52_out, not_53_out, in_1[2], in_1[1], not_54_out);
  and and_14 (and_14_out, not_55_out, not_56_out, not_57_out, not_58_out, in_1[3], not_59_out, in_1[1], in_1[0]);
  and and_15 (and_15_out, not_60_out, not_61_out, not_62_out, not_63_out, in_1[3], in_1[2], not_64_out, not_65_out);
  and and_16 (and_16_out, not_66_out, not_67_out, not_68_out, in_1[4], not_69_out, in_1[2], in_1[0]);
  and and_17 (and_17_out, not_70_out, not_71_out, not_72_out, in_1[4], not_73_out, in_1[2], in_1[1]);
  and and_18 (and_18_out, not_74_out, not_75_out, not_76_out, in_1[4], in_1[3], not_77_out, not_78_out);
  and and_19 (and_19_out, not_79_out, not_80_out, in_1[5], in_1[4], not_81_out, not_82_out, in_1[1], not_83_out);
  and and_20 (and_20_out, in_1[7], not_84_out, not_85_out, not_86_out, not_87_out, in_1[2], in_1[1], not_88_out);
  or or_1 (a, and_1_out, and_2_out, and_3_out, and_4_out, and_5_out);
  or or_2 (m, and_6_out, and_7_out, and_8_out, and_9_out, and_10_out, and_11_out, and_12_out, and_13_out);
  or or_3 (p, and_14_out, and_15_out, and_16_out, and_17_out, and_18_out, and_19_out, and_20_out);
endmodule
